// Digital circuit alu4_layout.dig as structural Verilog
module alu4_layout (
  input  Op1,
  input  Op0,
  input  compl_1,
  input  cin,
  input  A_3,
  input  A_2,
  input  A_1,
  input  A_0,
  input  B_3,
  input  B_2,
  input  B_1,
  input  B_0,
  output ZF,
  output CF,
  output OF,
  output SF,
  output S_3,
  output S_2,
  output S_1,
  output S_0
);

  // alu4 alu4_1: pin names not known; wires that end beside it: Op1, Op0, compl_1, cin, A_3, A_2, S_3, A_1, S_2, A_0, S_1, B_3, S_0, B_2, B_1, B_0, ZF, CF, OF, SF

  // Notes on the sheet:
  //   ZF: Flag de Zero - Se activa si el resultado es cero
  //   CF: Flag de acarreo - 
  //   Notifica el desbordamiento de aritmetica con naturales
  //   OF: Flag de overflow - 
  //   Notifica el desbordamiento de aritmetica con enteros
  //   SF: Flag de signo - Indica el signo del resultado
  //   S_3: Bit de orden 3 del resultado
  //   S_2: Bit de orden 2 del resultado
  //   S_1: Bit de orden 1 del resultado
  //   S_0: Bit de orden 0 del resultado
  //   Op1: Linea 1 de seleccion de operacion
  //   Op0: Linea 0 de seleccion de operacion
  //   compl_1: Linea de activacion del complemento a 1
  //   cin: Acarreo de entrada
  //   A_3: Bit de orden 3 del operando A
  //   A_2: Bit de orden 2 del operando A
  //   A_1: Bit de orden 1 del operando A
  //   A_0: Bit de orden 0 del operando A
  //   B_3: Bit de orden 3 del operando B
  //   B_2: Bit de orden 2 del operando B
  //   B_1: Bit de orden 1 del operando B
  //   B_0: Bit de orden 0 del operando B
endmodule
