// Digital circuit mux4.dig as structural Verilog
module mux4 (
  input  e_3,
  input  e_2,
  input  e_1,
  input  e_0,
  input  a_1,
  input  a_0,
  output S
);

  wire mux2_1_p2, mux2_2_p3;

  // mux2 mux2_1: pin names not known; wires that end beside it: e_0, mux2_1_p2, e_1, a_0
  // mux2 mux2_2: pin names not known; wires that end beside it: mux2_1_p2, S, mux2_2_p3, a_1
  // mux2 mux2_3: pin names not known; wires that end beside it: e_2, mux2_2_p3, e_3, a_0

  // Notes on the sheet:
  //   e_3: Entrada seleccionada con 3 (11)
  //   e_2: Entrada seleccionada con 2 (10)
  //   e_1: Entrada seleccionada con 1 (01)
  //   e_0: Entrada seleccionada con 0 (00)
  //   a_1: Linea de selección 1
  //   a_0: Linea de selección 0
  //   S: Salida multiplexor
endmodule
