// Digital circuit Eje2-boolean-function.dig as structural Verilog
module Eje2_boolean_function (
  input  E2,
  input  E1,
  input  E0,
  output S
);

  wire nor_1_out, or_1_out;

  nor nor_1 (nor_1_out, E2, E1);
  or or_1 (or_1_out, E2, E0);
  and and_1 (S, ~nor_1_out, or_1_out);  // And
endmodule

/* Test case:
E2	E1	E0	S
0	0	0	0
0	0	1	0
0	1	0	0
0	1	1	1
1	0	0	1
1	0	1	1
1	1	0	1
1	1	1	1
*/
