// Digital circuit datapath.dig as structural Verilog
module datapath (
  input  ALU_SR,
  input  ALU_TMPS,
  input  Op1,
  input  Op0,
  input  compl_1,
  input  cin,
  input  IB_3,
  input  IB_2,
  input  IB_1,
  input  IB_0,
  input  IB_TMPE,
  input  SR_IB,
  input  TMPS_IB,
  input  R1_IB,
  input  IB_R1,
  input  R0_IB,
  input  IB_R0,
  output S_3,
  output S_2,
  output S_1,
  output S_0
);

  wire alu4_1_p5, alu4_1_p6, alu4_1_p8, alu4_1_p10, alu4_1_p17, alu4_1_p18, alu4_1_p19, alu4_1_p20;

  // alu4 alu4_1: pin names not known; wires that end beside it: Op1, Op0, compl_1, cin, alu4_1_p5, alu4_1_p6, S_3, alu4_1_p8, S_2, alu4_1_p10, S_1, IB_3, S_0, IB_2, IB_1, IB_0, alu4_1_p17, alu4_1_p18, alu4_1_p19, alu4_1_p20
  reg4 reg4_1 (
    .Write(IB_TMPE), .e_3(IB_3), .e_2(IB_2), .e_1(IB_1), .e_0(IB_0), .s_3(alu4_1_p5), .s_2(alu4_1_p6),
    .s_1(alu4_1_p8), .s_0(alu4_1_p10));
  reg4_e_s reg4_e_s_1 (
    .Write(ALU_TMPS), .Read(TMPS_IB), .e_3(S_3), .e_2(S_2), .e_1(S_1), .e_0(S_0), .s_3(IB_3), .s_2(IB_2),
    .s_1(IB_1), .s_0(IB_0));
  reg4_e_s reg4_e_s_2 (
    .Write(ALU_SR), .Read(SR_IB), .e_3(alu4_1_p17), .e_2(alu4_1_p18), .e_1(alu4_1_p19), .e_0(alu4_1_p20),
    .s_3(IB_3), .s_2(IB_2), .s_1(IB_1), .s_0(IB_0));
  Paula_Register paula_register_1 (.Write(IB_R0), .Read(R0_IB), .d_3(IB_3), .d_2(IB_2), .d_1(IB_1), .d_0(IB_0));
  Paula_Register paula_register_2 (.Write(IB_R1), .Read(R1_IB), .d_3(IB_3), .d_2(IB_2), .d_1(IB_1), .d_0(IB_0));
endmodule
