// Digital circuit mux2.dig as structural Verilog
module mux2 (
  input  e_1,
  input  e_0,
  input  a_0,
  output S
);

  wire and_1_out, and_2_out, not_1_out;

  and and_1 (and_1_out, e_0, not_1_out);
  or or_1 (S, and_1_out, and_2_out);
  not not_1 (not_1_out, a_0);
  and and_2 (and_2_out, a_0, e_1);

  // Notes on the sheet:
  //   e_1: Entrada seleccionada con 1
  //   e_0: Entrada seleccionada con 0
  //   a_0: Linea de selección
  //   S: Salida del multiplexor
endmodule
