// Digital circuit alu4.dig as structural Verilog
module alu4 (
  input  Op1,
  input  Op0,
  input  compl_1,
  input  cin,
  input  A_3,
  input  A_2,
  input  A_1,
  input  A_0,
  input  B_3,
  input  B_2,
  input  B_1,
  input  B_0,
  output S_3,
  output S_2,
  output S_1,
  output S_0,
  output ZF,
  output CF,
  output OF,
  output SF
);

  wire alu4_nf_1_p17, xor_2_out;

  // alu4_nf alu4_nf_1: pin names not known; wires that end beside it: Op1, Op0, compl_1, cin, A_3, B_3, S_3, A_2, S_2, B_2, S_1, A_1, S_0, B_1, A_0, B_0, alu4_nf_1_p17
  nor nor_1 (ZF, S_3, S_2, S_1, S_0);
  xor xor_1 (CF, compl_1, alu4_nf_1_p17);
  gen_ov_s gen_ov_s_1 (.Ov(OF), .A_n_1(A_3), .B_n_1(xor_2_out), .S_n_1(S_3));
  xor xor_2 (xor_2_out, compl_1, B_3);

  assign SF = S_3;

  // Notes on the sheet:
  //   Op1: Linea 1 de seleccion de operacion
  //   Op0: Linea 0 de seleccion de operacion
  //   compl_1: Linea de activacion de complemento a 1
  //   cin: Acarreo de entrada
  //   A_3: Bit 3 del operando A
  //   A_2: Bit 2 del operando A
  //   A_1: Bit 1 del operando A
  //   A_0: Bit 0 del operando A
  //   B_3: Bit 3 del operando B
  //   B_2: Bit 2 del operando B
  //   B_1: Bit 1 del operando B
  //   B_0: Bit 0 del operando B
  //   S_3: Bit 3 del resultado
  //   S_2: Bit 2 del resultado
  //   S_1: Bit 1 del resultado
  //   S_0: Bit 0 del resultado
  //   ZF: Flag de Zero
  //   CF: Flag de acarreo
  //   OF: Flag de overflow
  //   SF: Flag de signo
endmodule
