// Digital circuit new-overflow.dig as structural Verilog
module new_overflow (
  input  A_n_1,
  input  B_n_1,
  input  S_n_1,
  output Ov
);

  wire and_1_out;

  Overflow overflow_1 (.A_n_1(A_n_1), .B_n_1(B_n_1), .S_n_1(S_n_1), .Ov(Ov));
  and and_1 (and_1_out, Ov, S_n_1);
  // Probe Signal on and_1_out
endmodule

/* Test case:
A_{n-1} B_{n-1} S_{n-1} Ov
0	0	0	0
0	0	1	1
0	1	0	0
0	1	1	0
1	0	0	0
1	0	1	0
1	1	0	1
1	1	1	0
*/
